# Fritzing sketch esp32 (saved by Fritzing 0.9.3b)
breadboards: 1

parts:
  hc-sr2 = hc-sr04
  MH-ET_LIVE_ESP32_DEVKIT2 = MH-ET LIVE ESP32 DEVKIT 38 pins
  LED4 = smd LED [color="Red (633nm)" package="0805 [SMD]"]
  LED5 = smd LED [color="Red (633nm)" package="0805 [SMD]"]
  LED6 = smd LED [color="Red (633nm)" package="0805 [SMD]"]
  R4 = Resistor [tolerance=±5% resistance=220 package="0805 [SMD]"]
  R5 = Resistor [tolerance=±5% resistance=220 package="0805 [SMD]"]
  R6 = Resistor [tolerance=±5% resistance=220 package="0805 [SMD]"]
  J2 = Basic Servo
  BT1 = Bluetooth HC-06u [package=THT]

nets:
  VCC: hc-sr2.VCC, MH-ET_LIVE_ESP32_DEVKIT2.5V, J2.vcc, BT1.VCC
  N1: hc-sr2.Trig, MH-ET_LIVE_ESP32_DEVKIT2.IO16
  N2: hc-sr2.Echo, MH-ET_LIVE_ESP32_DEVKIT2.IO17
  GND: hc-sr2.GND, MH-ET_LIVE_ESP32_DEVKIT2.GND, LED4.cathode, LED5.cathode, LED6.cathode, J2.gnd, BT1.GND
  N3: MH-ET_LIVE_ESP32_DEVKIT2.IO25, R6.Pin_0
  N4: MH-ET_LIVE_ESP32_DEVKIT2.IO26, R4.Pin_0
  N5: MH-ET_LIVE_ESP32_DEVKIT2.IO27, R5.Pin_0
  N6: MH-ET_LIVE_ESP32_DEVKIT2.IO19, BT1.RXD
  N7: MH-ET_LIVE_ESP32_DEVKIT2.IO18, BT1.TXD
  N8: LED4.anode, R5.Pin_1
  N9: LED5.anode, R4.Pin_1
  N10: LED6.anode, R6.Pin_1

custom parts:
  MH-ET LIVE ESP32 DEVKIT 38 pins: http://mh.nodebb.com/topic/2/mh-et-live-esp32-devkit
  Bluetooth HC-06u: Bluetooth HC-06 - face up, pins down 16.5mm x 37.5mm PCB
